# Fritzing sketch drone avec nano et hm10 (saved by Fritzing 0.9.3b)
circuit board: 18.0136cm x 11.5097cm
breadboards: 1

parts:
  Composant1 = Bluetooth HC-05 Macho
  M1 = DC Motor
  M2 = DC Motor
  U1 = POT [package=pot_alpha_rv16af-20]
  VCC3 = Battery
  VCC2 = Battery
  R1 = Resistor [tolerance=±5% resistance=220 package=THT]
  R2 = Resistor [tolerance=±5% resistance=220 package=THT]
  VCC1 = Battery
  Composant4 = Arduino Nano (Rev3.0)
  Composant5 = Logic Level Converter
  S2 = H-Bridge with L298N

nets:
  N1: Composant1.TXD, Composant5.RX2_LV
  N2: Composant1.RXD, Composant5.TX2_LV
  VCC: Composant1.VCC, Composant4.3V3, Composant5.LV
  GND: Composant1.GND, U1.A, VCC3.-, R2.Pin_0, Composant4.GND, Composant5.GND, S2.GND
  N3: M1.pin_1, S2.M2-02
  N4: M1.pin_2, S2.M2-01
  N5: M2.pin_1, S2.M1-02
  N6: M2.pin_2, S2.M1-01
  N7: U1.S, Composant4.A0
  5V: U1.E, Composant4.5V, Composant5.HV, S2.5V
  N8: VCC3.+, VCC2.-
  N9: VCC2.+, VCC1.-
  N10: R1.Pin_0, VCC1.+, S2.12V
  N11: R1.Pin_1, R2.Pin_1, Composant4.A1
  N12: Composant4.D2, Composant5.RX2_HV
  N13: Composant4.D3, Composant5.TX2_HV
  N14: Composant4.D4, S2.IN4
  N15: Composant4.D5, S2.IN3
  N16: Composant4.D6, S2.IN2
  N17: Composant4.D7, S2.IN1
  N18: S2.ENA, S2.ENB, S2.ENA-5V, S2.ENB-5V

notes:
  Moteur
  servo moteur
  AMpli et alim 5V
  Bluetooth
  diviseur de tension pour mesurer la tension batterie

custom parts:
  H-Bridge with L298N: h-bridge
