# Fritzing sketch drone avec nano (saved by Fritzing 0.9.3b)
breadboards: 1

parts:
  Composant1 = Bluetooth HC-05 Macho
  M1 = DC Motor
  M2 = DC Motor
  U1 = POT [package=pot_alpha_rv16af-20]
  VCC3 = Battery
  VCC2 = Battery
  Composant3 = Arduino Uno (Rev3) - ICSP
  R1 = Resistor [tolerance=±5% resistance=220 package=THT]
  R2 = Resistor [tolerance=±5% resistance=220 package=THT]
  VCC1 = Battery
  S1 = H-Bridge with L298N
  Composant4 = Arduino Nano (Rev3.0)  # not connected
  Composant5 = Logic Level Converter  # not connected

nets:
  N1: Composant1.TXD, Composant3.D2
  N2: Composant1.RXD, Composant3.D3_PWM
  5V: Composant1.VCC, U1.E, Composant3.5V, S1.5V
  GND: Composant1.GND, U1.A, VCC3.-, Composant3.GND, R2.Pin_0, S1.GND
  N3: M1.pin_1, S1.M2-02
  N4: M1.pin_2, S1.M2-01
  N5: M2.pin_1, S1.M1-02
  N6: M2.pin_2, S1.M1-01
  N7: U1.S, Composant3.A0
  N8: VCC3.+, VCC2.-
  N9: VCC2.+, VCC1.-
  N10: Composant3.A1, R1.Pin_1, R2.Pin_1
  N11: Composant3.D4, S1.IN1
  N12: Composant3.D5_PWM, S1.IN2
  N13: Composant3.D6_PWM, S1.IN3
  N14: Composant3.D7, S1.IN4
  N15: R1.Pin_0, VCC1.+, S1.12V

notes:
  Moteur
  servo moteur
  AMpli et alim 5V
  Bluetooth
  diviseur de tension pour mesurer la tension batterie

custom parts:
  H-Bridge with L298N: h-bridge
