# Fritzing sketch schéma sans spécificité (saved by Fritzing 0.9.3b)
breadboards: 1

parts:
  Composant1 = Bluetooth HC-05 Macho
  Composant3 = Arduino Uno (Rev3) - ICSP

nets:
  N1: Composant1.TXD, Composant3.D2
  N2: Composant1.RXD, Composant3.D3_PWM
  VCC: Composant1.VCC, Composant3.5V
  GND: Composant1.GND, Composant3.GND
