# Fritzing sketch schéma (saved by Fritzing 0.9.3b)
breadboards: 1

parts:
  Composant2 = Monster Moto Shield
  Composant1 = Bluetooth HC-05 Macho
  M1 = DC Motor
  M2 = DC Motor
  U1 = POT [package=pot_alpha_rv16af-20]
  VCC3 = Battery
  VCC2 = Battery
  Composant3 = Arduino Uno (Rev3) - ICSP
  R1 = Resistor [tolerance=±5% resistance=220 package=THT]
  R2 = Resistor [tolerance=±5% resistance=220 package=THT]
  VCC1 = Battery

nets:
  N1: Composant2.OUTA1, M1.pin_1
  N2: Composant2.OUTB1, M1.pin_2
  N3: Composant2.OUTA2, M2.pin_1
  N4: Composant2.OUTB2, M2.pin_2
  N5: Composant2.VCC, R1.Pin_0, VCC1.+
  GND: Composant2.GND, Composant1.GND, U1.A, VCC3.-, Composant3.GND, R2.Pin_0
  5V: Composant2.5V, Composant1.VCC, U1.E, Composant3.5V
  N6: Composant2.D2, Composant3.D4
  N7: Composant2.D3, Composant3.D5_PWM
  N8: Composant2.INA2_-_D4, Composant3.D6_PWM
  N9: Composant2.PWM1_-_D5, Composant3.D7
  N10: Composant1.TXD, Composant3.D2
  N11: Composant1.RXD, Composant3.D3_PWM
  N12: U1.S, Composant3.A0
  N13: VCC3.+, VCC2.-
  N14: VCC2.+, VCC1.-
  N15: Composant3.A1, R1.Pin_1, R2.Pin_1

notes:
  Moteur
  servo moteur
  AMpli et alim 5V
  Bluetooth
